// Logisim project final_logisim.circ as structural Verilog: 1 circuit, main circuit main
module main (
  input  in_1
);

  wire and_1_out, and_2_out, and_3_out, and_4_out, and_5_out, and_6_out, and_7_out, and_8_out, and_9_out,
       and_10_out, and_11_out, and_12_out, and_13_out, and_14_out, and_15_out, clock_1_out, decoder_1_out0,
       decoder_1_out1, decoder_1_out2, decoder_1_out3, t_ff_1_q, t_ff_2_q, t_ff_3_q, t_ff_4_q, t_ff_5_q,
       t_ff_6_q;
  wire [2:0] bcd_to_7_segment_decoder_1_p1, bcd_to_7_segment_decoder_3_p1, counter_2_q, counter_4_q;
  wire [3:0] bcd_to_7_segment_decoder_2_p1, bcd_to_7_segment_decoder_4_p1, bcd_to_7_segment_decoder_5_p2,
       bcd_to_7_segment_decoder_6_p1, bcd_to_7_segment_decoder_7_p1, bcd_to_7_segment_decoder_8_p1,
       counter_1_q, multiplexer_4_out, undriven;

  Clock clock_1 (.out(clock_1_out));
  T_Flip_Flop t_ff_1 (.T(in_1), .clk(clock_1_out), .Q(t_ff_1_q));  // open: Qn, reset, preset
  and and_1 (and_1_out, in_1, t_ff_1_q);
  T_Flip_Flop t_ff_2 (.T(and_1_out), .clk(clock_1_out), .Q(t_ff_2_q));  // open: Qn, reset, preset
  _7_Segment_Display u_7_segment_display_1 ();  // open: g, f, a, b, e, d, c, dp
  // BCD_to_7_Segment_decoder bcd_to_7_segment_decoder_1: pin names not known; wires that end beside it: {1'b0, bcd_to_7_segment_decoder_1_p1}
  and and_2 (and_2_out, and_1_out, t_ff_2_q);
  T_Flip_Flop t_ff_3 (.T(and_2_out), .clk(clock_1_out), .Q(t_ff_3_q));  // open: Qn, reset, preset
  Counter #(.max('hf), .width(4)) counter_1 (
    .up(1'b1), .count(and_6_out), .clk(t_ff_6_q), .Q(counter_1_q));  // open: clr, load, D, carry
  _7_Segment_Display u_7_segment_display_2 ();  // open: g, f, a, b, e, d, c, dp
  // BCD_to_7_Segment_decoder bcd_to_7_segment_decoder_2: pin names not known; wires that end beside it: bcd_to_7_segment_decoder_2_p1
  and and_3 (and_3_out, and_2_out, t_ff_3_q);
  T_Flip_Flop t_ff_4 (.T(and_3_out), .clk(clock_1_out), .Q(t_ff_4_q));  // open: Qn, reset, preset
  _7_Segment_Display u_7_segment_display_3 ();  // open: g, f, a, b, e, d, c, dp
  // BCD_to_7_Segment_decoder bcd_to_7_segment_decoder_3: pin names not known; wires that end beside it: {1'b0, bcd_to_7_segment_decoder_3_p1}
  and and_4 (and_4_out, and_3_out, t_ff_4_q);
  Counter #(.max('h7), .width(3)) counter_2 (
    .up(1'b1), .count(1'b1), .clk(t_ff_6_q), .Q(counter_2_q));  // open: clr, load, D, carry
  T_Flip_Flop t_ff_5 (.T(and_4_out), .clk(clock_1_out), .Q(t_ff_5_q));  // open: Qn, reset, preset
  _7_Segment_Display u_7_segment_display_4 ();  // open: g, f, a, b, e, d, c, dp
  // BCD_to_7_Segment_decoder bcd_to_7_segment_decoder_4: pin names not known; wires that end beside it: bcd_to_7_segment_decoder_4_p1
  and and_5 (and_5_out, and_4_out, t_ff_5_q);
  T_Flip_Flop t_ff_6 (.T(and_5_out), .clk(clock_1_out), .Q(t_ff_6_q));  // open: Qn, reset, preset
  and and_6 (and_6_out, counter_2_q[0], counter_2_q[1], counter_2_q[2]);
  Counter #(.max('h7), .width(3)) counter_3 (
    .clr(and_7_out), .count(and_8_out), .clk(counter_1_q[3]), .Q(bcd_to_7_segment_decoder_1_p1));  // open: load, up, D, carry
  Counter #(.max('h7), .width(3)) counter_4 (
    .clr(counter_4_q[2]), .clk(clock_1_out), .Q(counter_4_q));  // open: load, up, count, D, carry
  and and_7 (and_7_out, bcd_to_7_segment_decoder_1_p1[1], bcd_to_7_segment_decoder_1_p1[2]);
  and and_8 (and_8_out, and_13_out, and_10_out);
  Counter #(.max('hf), .width(4)) counter_5 (
    .clr(and_9_out), .count(and_13_out), .clk(counter_1_q[3]), .Q(bcd_to_7_segment_decoder_2_p1));  // open: load, up, D, carry
  _7_Segment_Display u_7_segment_display_5 ();  // open: g, f, a, b, e, d, c, dp
  // BCD_to_7_Segment_decoder bcd_to_7_segment_decoder_5: pin names not known; wires that end beside it: counter_4_q, bcd_to_7_segment_decoder_5_p2
  Multiplexer #(.width(4)) multiplexer_1 (
    .in0(undriven), .in1(multiplexer_4_out), .out(bcd_to_7_segment_decoder_5_p2), .sel(decoder_1_out3));
  _7_Segment_Display u_7_segment_display_6 ();  // open: g, f, a, b, e, d, c, dp
  // BCD_to_7_Segment_decoder bcd_to_7_segment_decoder_6: pin names not known; wires that end beside it: bcd_to_7_segment_decoder_6_p1
  Decoder #(.select(2)) decoder_1 (
    .out0(decoder_1_out0), .out1(decoder_1_out1), .out2(decoder_1_out2), .out3(decoder_1_out3),
    .sel(counter_4_q[1:0]), .en(1'b1));
  Multiplexer #(.width(4)) multiplexer_2 (
    .in0(undriven), .in1(multiplexer_4_out), .out(bcd_to_7_segment_decoder_6_p1), .sel(decoder_1_out2));
  and and_9 (and_9_out, bcd_to_7_segment_decoder_2_p1[1], bcd_to_7_segment_decoder_2_p1[3]);
  _7_Segment_Display u_7_segment_display_7 ();  // open: g, f, a, b, e, d, c, dp
  // BCD_to_7_Segment_decoder bcd_to_7_segment_decoder_7: pin names not known; wires that end beside it: bcd_to_7_segment_decoder_7_p1
  Multiplexer #(.width(4)) multiplexer_3 (
    .in0(undriven), .in1(multiplexer_4_out), .out(bcd_to_7_segment_decoder_7_p1), .sel(decoder_1_out1));
  Multiplexer #(.select(2), .width(4)) multiplexer_4 (
    .in0(bcd_to_7_segment_decoder_4_p1), .in1({1'b0, bcd_to_7_segment_decoder_3_p1}),
    .in2(bcd_to_7_segment_decoder_2_p1), .in3({1'b0, bcd_to_7_segment_decoder_1_p1}),
    .out(multiplexer_4_out), .sel(counter_4_q[1:0]));
  and and_10 (and_10_out, bcd_to_7_segment_decoder_2_p1[3], bcd_to_7_segment_decoder_2_p1[0]);
  _7_Segment_Display u_7_segment_display_8 ();  // open: g, f, a, b, e, d, c, dp
  // BCD_to_7_Segment_decoder bcd_to_7_segment_decoder_8: pin names not known; wires that end beside it: bcd_to_7_segment_decoder_8_p1
  Multiplexer #(.width(4)) multiplexer_5 (
    .in0(undriven), .in1(multiplexer_4_out), .out(bcd_to_7_segment_decoder_8_p1), .sel(decoder_1_out0));
  Counter #(.max('h7), .width(3)) counter_6 (
    .clr(and_11_out), .up(1'b1), .count(and_15_out), .clk(counter_1_q[3]), .Q(bcd_to_7_segment_decoder_3_p1));  // open: load, D, carry
  and and_11 (and_11_out, bcd_to_7_segment_decoder_3_p1[1], bcd_to_7_segment_decoder_3_p1[2]);
  and and_12 (and_12_out, bcd_to_7_segment_decoder_3_p1[2], bcd_to_7_segment_decoder_3_p1[0]);
  and and_13 (and_13_out, and_12_out, and_15_out);
  Counter #(.max('hf), .width(4)) counter_7 (
    .clr(and_14_out), .up(1'b1), .count(1'b1), .clk(counter_1_q[3]), .Q(bcd_to_7_segment_decoder_4_p1));  // open: load, D, carry
  // Probe on counter_1_q[3]
  and and_14 (and_14_out, bcd_to_7_segment_decoder_4_p1[1], bcd_to_7_segment_decoder_4_p1[3]);
  and and_15 (and_15_out, bcd_to_7_segment_decoder_4_p1[0], bcd_to_7_segment_decoder_4_p1[3]);

  // Notes on the sheet:
  //   The CLOCK
endmodule
