// Logisim project logism_alarm (1).circ as structural Verilog: 1 circuit, main circuit main
module main (
  input  en,
  input  [3:0] in_2,
  input  [3:0] in_3,
  input  [2:0] in_4,
  input  [2:0] in_5,
  input  [2:0] in_6,
  input  [2:0] in_7,
  input  [1:0] in_8,
  input  [3:0] in_9
);

  wire and_1_out, and_2_out, and_3_out, and_4_out, and_5_out, and_6_out, and_7_out, button_1_out,
       clock_1_out, counter3_2_carry, counter3_carry, counter4_carry, counter_1_carry, counter_2_carry,
       counterfour_carry, not_1_out, not_2_out, not_3_out, or_1_out, or_2_out, or_3_out, or_4_out, or_5_out;
  wire [1:0] counter_1_q;
  wire [2:0] counter3_2_q, counter3_q;
  wire [3:0] bit_extender_1_out, counter4_q, counter_2_q, counterfour_q, n7_segment_display_3_p1,
       n7_segment_display_5_p1;

  Clock clock_1 (.out(clock_1_out));
  Counter #(.max('h2), .width(2)) counter_1 (
    .clr(button_1_out), .load(or_2_out), .count(and_6_out), .clk(clock_1_out), .D(in_8),
    .carry(counter_1_carry), .Q(counter_1_q));  // open: up
  Button button_1 (.out(button_1_out));
  or or_1 (or_1_out, and_3_out, and_1_out);
  Counter #(.max('h9), .width(4)) counter4 (
    .clr(button_1_out), .load(counter4_carry), .count(en), .clk(clock_1_out), .D(in_2),
    .carry(counter4_carry), .Q(counter4_q));  // open: up
  Counter #(.max('h5), .width(3)) counter3 (
    .clr(button_1_out), .load(or_1_out), .count(counter4_carry), .clk(clock_1_out), .D(in_4),
    .carry(counter3_carry), .Q(counter3_q));  // open: up
  and and_1 (and_1_out, counter_1_carry, and_5_out);
  or or_2 (or_2_out, and_1_out, and_2_out);
  and and_2 (and_2_out, counter_1_carry, and_6_out);
  and and_3 (and_3_out, counter3_carry, counter4_carry);
  assign bit_extender_1_out = {{2{1'b0}}, counter_1_q};  // Bit_Extender bit_extender_1
  or or_3 (or_3_out, and_6_out, and_1_out);
  Counter #(.max('h9), .width(4)) counter_2 (
    .clr(button_1_out), .load(or_3_out), .count(and_7_out), .clk(clock_1_out), .D(in_9),
    .carry(counter_2_carry), .Q(counter_2_q));  // open: up
  and and_4 (and_4_out, and_3_out, counterfour_carry);
  Counter #(.max('h9), .width(4)) counterfour (
    .clr(button_1_out), .load(or_5_out), .count(and_3_out), .clk(clock_1_out), .D(in_3),
    .carry(counterfour_carry), .Q(counterfour_q));  // open: up
  Counter #(.max('h5), .width(3)) counter3_2 (
    .clr(button_1_out), .load(or_4_out), .count(and_4_out), .clk(clock_1_out), .D(in_7),
    .carry(counter3_2_carry), .Q(counter3_2_q));  // open: up
  // _7_Segment_Display 7_segment_display_1: pin names not known; wires that end beside it: bit_extender_1_out, counter_2_q
  // BCD_to_7_Segment_decoder bcd_to_7_segment_decoder_1: pin names not known
  not not_1 (not_1_out, counter_2_q[3]);
  not not_2 (not_2_out, counter_2_q[1]);
  and and_5 (and_5_out, not_1_out, not_2_out, counter_2_q[2], not_3_out);
  _7_Segment_Display u_7_segment_display_2 ();  // open: g, f, a, b, e, d, c, dp
  // _7_Segment_Display 7_segment_display_3: pin names not known; wires that end beside it: n7_segment_display_3_p1, counterfour_q
  // BCD_to_7_Segment_decoder bcd_to_7_segment_decoder_2: pin names not known
  // BCD_to_7_Segment_decoder bcd_to_7_segment_decoder_3: pin names not known
  and and_6 (and_6_out, counter_2_carry, and_7_out);
  not not_3 (not_3_out, counter_2_q[0]);
  _7_Segment_Display u_7_segment_display_4 ();  // open: g, f, a, b, e, d, c, dp
  // BCD_to_7_Segment_decoder bcd_to_7_segment_decoder_4: pin names not known
  and and_7 (and_7_out, counter3_2_carry, and_4_out);
  // _7_Segment_Display 7_segment_display_5: pin names not known; wires that end beside it: n7_segment_display_5_p1, counter4_q
  // BCD_to_7_Segment_decoder bcd_to_7_segment_decoder_5: pin names not known
  _7_Segment_Display u_7_segment_display_6 ();  // open: g, f, a, b, e, d, c, dp
  // BCD_to_7_Segment_decoder bcd_to_7_segment_decoder_6: pin names not known
  assign n7_segment_display_3_p1 = {{1{1'b0}}, counter3_2_q};  // Bit_Extender bit_extender_2
  or or_4 (or_4_out, and_7_out, and_1_out);
  assign n7_segment_display_5_p1 = {{1{1'b0}}, counter3_q};  // Bit_Extender bit_extender_3
  or or_5 (or_5_out, and_4_out, and_1_out);

  // Notes on the sheet:
  //   rst
endmodule
